# Fritzing sketch domotica (saved by Fritzing 0.9.3b)
breadboards: 1

parts:
  Grove2 = Grove Infrared Receiver
  LED2 = smd LED [color="Yellow (595nm)" package="0805 [SMD]"]
  R3 = Resistor [tolerance=±5% resistance=220 package="0805 [SMD]"]
  Part3 = Breakout Board for Electret Microphone
  Q2 = NPN-Transistor [package="SOT-23 [SMD]"]
  M2 = DC Motor
  R4 = Resistor [tolerance=±5% resistance=220 package="1206 [SMD]"]
  D3 = Rectifier Diode 10A [part_number=P1000K]
  Part4 = Arduino Uno (Rev3)

nets:
  GND: Grove2.GND, LED2.cathode, Part3.GND, Q2.2, Part4.GND
  VCC: Grove2.VCC, Part3.VCC, Part4.3V3
  N1: Grove2.RX, Part4.D7
  N2: LED2.anode, R3.Pin_0
  N3: R3.Pin_1, Part4.D5_PWM
  N4: Part3.AUD, Part4.A5/SCL
  N5: Q2.0, R4.Pin_1
  N6: Q2.1, M2.pin_2, D3.anode
  N7: M2.pin_1, D3.cathode, Part4.5V
  N8: R4.Pin_0, Part4.D3_PWM
