# Fritzing sketch cerrojo (saved by Fritzing 0.9.3b)
breadboards: 1

parts:
  Part1 = Arduino Uno (Rev3)
  Matrix_keypad1 = KEYPAD 4x4
  LED1 = smd LED [color="Red (633nm)" package="0603 [SMD]"]
  LED2 = smd LED [color="Blue (525nm)" package="0603 [SMD]"]
  J1 = Piezo Speaker
  R1 = Resistor [tolerance=±5% resistance=220 package="2512 [SMD]"]
  R2 = Resistor [tolerance=±5% resistance=220 package="2512 [SMD]"]

nets:
  N1: Part1.D8, Matrix_keypad1.col1
  N2: Part1.D9_PWM, Matrix_keypad1.col2
  N3: Part1.D10_PWM/SS, Matrix_keypad1.col3
  N4: Part1.D11_PWM/MOSI, Matrix_keypad1.col4
  N5: Part1.D0/RX, R1.Pin_1
  N6: Part1.D1/TX, R2.Pin_1
  N7: Part1.D2, J1.pin2
  N8: Part1.D4, Matrix_keypad1.row1
  N9: Part1.D5_PWM, Matrix_keypad1.row2
  N10: Part1.D6_PWM, Matrix_keypad1.row3
  N11: Part1.D7, Matrix_keypad1.row4
  N12: Part1.GND, LED1.cathode, LED2.cathode, J1.pin1
  N13: LED1.anode, R2.Pin_0
  N14: LED2.anode, R1.Pin_0

custom parts:
  KEYPAD 4x4: Matrix keypad 16 buttons, 4 rows x 4 columns
